# Fritzing sketch DemoSetUp (saved by Fritzing 0.9.4)
breadboards: 2

parts:
  OLED_I2C1 = OLED 128x64 I2C Monochrome Display
  OLED_I2C2 = OLED 128x64 I2C Monochrome Display
  OLED_I2C3 = OLED 128x64 I2C Monochrome Display
  LED1 = smd LED [color="White (4500K)" package="0603 [SMD]"]
  LED2 = smd LED [color="Blue (525nm)" package="0805 [SMD]"]
  R1 = Resistor [tolerance=±5% resistance=681 package=THT]
  R2 = Resistor [tolerance=±5% resistance=681 package=THT]
  LED3 = smd LED [color="Green (565nm)" package="0805 [SMD]"]
  LED4 = smd LED [color="Red (635nm)" package="0805 [SMD]"]
  R3 = Resistor [tolerance=±5% resistance=681 package=THT]
  R4 = Resistor [tolerance=±5% resistance=681 package=THT]
  WeMos_D1_Mini4 = WeMos D1 Mini
  WeMos_D1_Mini3 = WeMos D1 Mini
  WeMos_D1_Mini1 = WeMos D1 Mini
  WeMos_D1_Mini2 = WeMos D1 Mini
  S1 = Momentary Switch [package=ksa_sealed_tac_switch]
  S2 = Momentary Switch [package=ksa_sealed_tac_switch]
  S3 = Momentary Switch [package=ksa_sealed_tac_switch]
  R5 = Resistor [tolerance=±5% resistance=10k package=THT]  # not connected
  R6 = Resistor [tolerance=±5% resistance=10k package=THT]
  R7 = Resistor [tolerance=±5% resistance=10k package=THT]

nets:
  N1: OLED_I2C1.SDA, WeMos_D1_Mini2.D1
  N2: OLED_I2C1.SCK, WeMos_D1_Mini2.D2
  VDD: OLED_I2C1.VDD, OLED_I2C2.VDD
  GND: OLED_I2C1.GND, OLED_I2C2.GND, LED1.cathode, WeMos_D1_Mini4.G, WeMos_D1_Mini2.G, S3.3
  N3: OLED_I2C2.SDA, WeMos_D1_Mini4.D1
  N4: OLED_I2C2.SCK, WeMos_D1_Mini4.D2
  N5: OLED_I2C3.SDA, WeMos_D1_Mini3.D1
  N6: OLED_I2C3.SCK, WeMos_D1_Mini3.D2
  VDD_2: OLED_I2C3.VDD, WeMos_D1_Mini1.3V3, R6.Pin_0, R7.Pin_0
  N7: OLED_I2C3.GND, WeMos_D1_Mini3.G, S1.3, S2.3
  N8: LED1.anode, R2.Pin_0
  N9: LED2.cathode, LED3.cathode, LED4.cathode, WeMos_D1_Mini1.G
  N10: LED2.anode, R1.Pin_1
  N11: R1.Pin_0, WeMos_D1_Mini1.D6
  N12: R2.Pin_1, WeMos_D1_Mini2.D0
  N13: LED3.anode, R3.Pin_1
  N14: LED4.anode, R4.Pin_1
  N15: R3.Pin_0, WeMos_D1_Mini1.D5
  N16: R4.Pin_0, WeMos_D1_Mini1.D0
  3V3: WeMos_D1_Mini4.3V3, WeMos_D1_Mini2.3V3
  N17: WeMos_D1_Mini4.D5, S3.2
  N18: WeMos_D1_Mini3.D0, S1.2
  N19: WeMos_D1_Mini3.D5, S2.2
  N20: WeMos_D1_Mini1.RX, WeMos_D1_Mini2.TX
  N21: WeMos_D1_Mini1.TX, WeMos_D1_Mini2.RX
  N22: S1.1, R6.Pin_1
  N23: S2.1, R7.Pin_1
